# Fritzing sketch JavaArduino (saved by Fritzing 0.9.2b)
breadboards: 1

parts:
  Parte1 = Arduino Uno (Rev3) - ICSP
  LCD1 = LCD screen
  R1 = Trimmer Potentiometer [maximum_resistance=10kΩ package=THT]
  R2 = Resistor [tolerance=±5% resistance=220 package=THT]
  S2 = Pushbutton [package=THT]
  S3 = Pushbutton [package=THT]
  R3 = Resistor [tolerance=±5% resistance=220 package=THT]
  T1 = LM35 Temperature Sensor [package="TO92 [THT]"]
  R4 = Resistor [tolerance=±5% resistance=220 package=THT]
  J1 = Piezo Speaker

nets:
  N1: Parte1.A0, T1.Vout
  N2: Parte1.ICSP_MISO, Parte1.D12/MISO, LCD1.RS
  N3: Parte1.ICSP_MOSI, Parte1.D11_PWM/MOSI, LCD1.E
  N4: Parte1.D8, S3.leg1, R3.Pin_1
  N5: Parte1.D9_PWM, S2.leg1, R4.Pin_1
  N6: Parte1.D1/TX, J1.pin2
  N7: Parte1.D2, LCD1.DB7
  N8: Parte1.D3_PWM, LCD1.DB6
  N9: Parte1.D4, LCD1.DB5
  N10: Parte1.D5_PWM, LCD1.DB4
  5V: Parte1.5V, LCD1.VDD, R1.leg2, R2.Pin_0, S2.leg0, S3.leg0, T1.+Vs
  GND: Parte1.GND, LCD1.VSS, LCD1.R/W, LCD1.LED-, R1.leg1, R3.Pin_0, T1.GND, R4.Pin_0, J1.pin1
  N11: LCD1.V0, R1.wiper
  N12: LCD1.LED+, R2.Pin_1
